# Fritzing sketch Untitled Sketch (saved by Fritzing 0.9.3b)
breadboards: 1

parts:
  元件1 = Arduino Uno (Rev3)
  PIR = IR Receiver Breakout [package=PCB]
  IR2 = TSOP312.., 314.. [package=THT]
  1kΩ = Resistor [tolerance=±5% resistance=220 package=THT]
  R1 = Photocell (LDR) [package=THT]

nets:
  N1: 元件1.A5/SCL, 1kΩ.Pin_1, R1.pin_1
  N2: 元件1.D9_PWM, PIR.OUT
  N3: 元件1.D3_PWM, IR2.data
  VCC: 元件1.5V, PIR.VCC, IR2.VCC, 1kΩ.Pin_0
  GND: 元件1.GND, PIR.GND, IR2.GND, R1.pin_0

custom parts:
  TSOP312.., 314..: The TSOP312.., TSOP314.. series are miniaturized receivers for infrared remote control systems. A PIN diode and a preamplifier are assembled on a lead frame, the epoxy package acts as an IR filter. The demodulated output signal can be directly decoded by a microprocessor. The TSOP312.. is compatible with all common IR remote control data formats. The TSOP314.. is optimized to suppress almost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
