# Fritzing sketch 主机v1.0 (saved by Fritzing 0.9.3b)
breadboards: 1

parts:
  元件1 = Arduino Uno (Rev3)
  超时波测距 = hc-sr04
  光敏电阻 = Photocell (LDR) [package=THT]
  红外信号接收端 = TSOP312.., 314.. [package=THT]
  元件2 = Motor Driver 1A Dual TB6612FNG
  LED3 = smd LED [color="Red (633nm)" package="0805 [SMD]"]
  LED4 = smd LED [color="Red (633nm)" package="0805 [SMD]"]
  元件3 = Arduino Uno (Rev3)
  元件4 = Motor Driver 1A Dual TB6612FNG
  LED5 = smd LED [color="Red (633nm)" package="0805 [SMD]"]
  LED6 = smd LED [color="Red (633nm)" package="0805 [SMD]"]

nets:
  N1: 元件1.A0, 光敏电阻.pin_0
  N2: 元件1.D8, 元件2.BIN1
  N3: 元件1.D9_PWM, 元件2.BIN2
  N4: 元件1.D10_PWM/SS, 元件2.PWMB
  N5: 元件1.D11_PWM/MOSI, 元件2.PWMA
  N6: 元件1.D12/MISO, 元件2.AIN2
  N7: 元件1.D13/SCK, 元件2.AIN1
  GND: 元件1.GND, 超时波测距.GND, 红外信号接收端.GND, 元件2.GND, 元件4.GND
  N8: 元件1.D0/RX, 元件3.D1/TX
  N9: 元件1.D1/TX, 元件3.D0/RX
  N10: 元件1.D3_PWM, 红外信号接收端.Data
  N11: 元件1.D5_PWM, 超时波测距.Echo
  N12: 元件1.D6_PWM, 超时波测距.Trig
  VCC: 元件1.5V, 超时波测距.VCC, 光敏电阻.pin_1, 红外信号接收端.VCC, 元件2.VCC, 元件2.STBY, 元件4.VCC, 元件4.STBY
  N13: 元件1.VIN, 元件2.VM, 元件4.VM
  N14: 元件2.B01, LED3.anode
  N15: 元件2.B02, LED3.cathode
  N16: 元件2.A02, LED4.cathode
  N17: 元件2.A01, LED4.anode
  N18: 元件3.D8, 元件4.PWMB
  N19: 元件3.D9_PWM, 元件4.BIN2
  N20: 元件3.D10_PWM/SS, 元件4.BIN1
  N21: 元件3.D11_PWM/MOSI, 元件4.PWMA
  N22: 元件3.D12/MISO, 元件4.AIN2
  N23: 元件3.D13/SCK, 元件4.AIN1
  N24: 元件4.B01, LED6.anode
  N25: 元件4.B02, LED6.cathode
  N26: 元件4.A02, LED5.cathode
  N27: 元件4.A01, LED5.anode

custom parts:
  TSOP312.., 314..: The TSOP312.., TSOP314.. series are miniaturized receivers for infrared remote control systems. A PIN diode and a preamplifier are assembled on a lead frame, the epoxy package acts as an IR filter. The demodulated output signal can be directly decoded by a microprocessor. The TSOP312.. is compatible with all common IR remote control data formats. The TSOP314.. is optimized to suppress almost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
