# Fritzing sketch 主机v2.0 (saved by Fritzing 0.9.3b)
breadboards: 2

parts:
  元件1 = Arduino Uno (Rev3)
  超时波测距 = hc-sr04
  光敏电阻 = Photocell (LDR) [package=THT]
  红外信号接收端 = TSOP312.., 314.. [package=THT]
  元件2 = Motor Driver 1A Dual TB6612FNG
  LED3 = smd LED [color="Red (633nm)" package="0805 [SMD]"]
  LED4 = smd LED [color="Red (633nm)" package="0805 [SMD]"]
  元件3 = Arduino Uno (Rev3)
  LCD1 = LCD screen
  IR1 = TSOP312.., 314.. [package=THT]
  R1 = Rotary Potentiometer (Small) [maximum_resistance=100kΩ package=THT]

nets:
  N1: 元件1.A5/SCL, 光敏电阻.pin_0
  N2: 元件1.D8, 元件2.BIN1
  N3: 元件1.D9_PWM, 元件2.BIN2
  N4: 元件1.D10_PWM/SS, 元件2.PWMB
  N5: 元件1.D11_PWM/MOSI, 元件2.PWMA
  N6: 元件1.D12/MISO, 元件2.AIN2
  N7: 元件1.D13/SCK, 元件2.AIN1
  N8: 元件1.D0/RX, 元件3.D1/TX
  N9: 元件1.D1/TX, 元件3.D0/RX
  N10: 元件1.D3_PWM, 红外信号接收端.Data
  N11: 元件1.D5_PWM, 超时波测距.Echo
  N12: 元件1.D6_PWM, 超时波测距.Trig
  VCC: 元件1.5V, 超时波测距.VCC, 光敏电阻.pin_1, 红外信号接收端.VCC, 元件2.VCC, 元件2.STBY
  GND: 元件1.GND, 超时波测距.GND, 红外信号接收端.GND, 元件2.GND
  N13: 元件1.VIN, 元件2.VM
  N14: 元件2.B01, LED3.anode
  N15: 元件2.B02, LED3.cathode
  N16: 元件2.A02, LED4.cathode
  N17: 元件2.A01, LED4.anode
  N18: 元件3.D9_PWM, IR1.data
  N19: 元件3.D11_PWM/MOSI, LCD1.E
  N20: 元件3.D12/MISO, LCD1.RS
  N21: 元件3.D2, LCD1.DB7
  N22: 元件3.D3_PWM, LCD1.DB6
  N23: 元件3.D4, LCD1.DB5
  N24: 元件3.D5_PWM, LCD1.DB4
  N25: 元件3.D6_PWM, LCD1.LED+
  5V: 元件3.5V, LCD1.VDD, IR1.VCC, R1.leg2
  GND_2: 元件3.GND, LCD1.VSS, LCD1.R/W, LCD1.LED-, IR1.GND, R1.leg1
  N26: LCD1.V0, R1.wiper

custom parts:
  TSOP312.., 314..: The TSOP312.., TSOP314.. series are miniaturized receivers for infrared remote control systems. A PIN diode and a preamplifier are assembled on a lead frame, the epoxy package acts as an IR filter. The demodulated output signal can be directly decoded by a microprocessor. The TSOP312.. is compatible with all common IR remote control data formats. The TSOP314.. is optimized to suppress almost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
  TSOP312.., 314..: The TSOP312.., TSOP314.. series are miniaturized receivers for infrared remote control systems. A PIN diode and a preamplifier are assembled on a lead frame, the epoxy package acts as an IR filter. The demodulated output signal can be directly decoded by a microprocessor. The TSOP312.. is compatible with all common IR remote control data formats. The TSOP314.. is optimized to suppress almost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
